# Fritzing sketch ControlPanel (saved by Fritzing 0.9.0b)
circuit board: 8.46667cm x 5.64444cm
breadboards: 1

parts:
  Raspberry_Pi_3 = Raspberry Pi 3
  S1 = Toggle Switch [package=THT]
  S2 = Toggle Switch [package=THT]
  S3 = Toggle Switch [package=THT]
  R1 = Resistor [tolerance=±5% resistance=220 package=THT]
  R2 = Resistor [tolerance=±5% resistance=220 package=THT]
  R3 = Resistor [tolerance=±5% resistance=220 package=THT]
  U1 = LCD-16X2 [package=lcd-16x2]

nets:
  3V3: Raspberry_Pi_3.3v3, Raspberry_Pi_3.3V3, S1.COM, S2.COM, S3.COM, U1.VDD
  N1: Raspberry_Pi_3.GIPO4, U1.E
  N2: Raspberry_Pi_3.GIPO17, U1.RS
  N3: Raspberry_Pi_3.GIPO5, U1.DB4
  N4: Raspberry_Pi_3.GIPO6, U1.DB5
  N5: Raspberry_Pi_3.GIPO13, U1.DB6
  N6: Raspberry_Pi_3.GIPO19, U1.DB7
  GND: Raspberry_Pi_3.GND, U1.VSS, U1.R_W
  N7: Raspberry_Pi_3.GIPO25, R1.Pin_0
  N8: Raspberry_Pi_3.GIPO24, R2.Pin_0
  N9: Raspberry_Pi_3.GIPO23, R3.Pin_0
  N10: S1.L2, R1.Pin_1
  N11: S2.L2, R2.Pin_1
  N12: S3.L2, R3.Pin_1
